// Logisim project CALCULATOR (2).circ as structural Verilog: 1 circuit, main circuit main
module main (
  input  [3:0] in_1,
  input  in_2,
  input  [3:0] in_3,
  input  [3:0] in_4,
  input  [3:0] in_5,
  input  [3:0] in_6,
  input  [3:0] in_7,
  input  [3:0] in_8,
  input  [3:0] in_9,
  input  [3:0] in_10,
  input  [3:0] in_11,
  input  [3:0] in_12,
  input  [3:0] in_13,
  input  [3:0] in_14,
  input  [3:0] in_15,
  input  [3:0] in_16,
  input  [3:0] in_17,
  input  [3:0] in_18,
  input  [3:0] in_19,
  input  [3:0] in_20,
  output [3:0] out_21,
  output [3:0] out_22,
  output [3:0] out_23,
  output [3:0] out_24,
  output [3:0] out_25,
  output [3:0] out_26,
  output [3:0] out_27,
  output [3:0] out_28,
  output out_29,
  output out_30,
  output out_31,
  output [3:0] out_32,
  output [3:0] out_33,
  output [3:0] out_34,
  output [3:0] out_35,
  output [3:0] out_36,
  output [3:0] out_37,
  output [3:0] out_38,
  output [3:0] out_39,
  output [3:0] out_40,
  output [3:0] out_41,
  output out_42,
  output out_43
);

  wire adder_1_cout, adder_2_cout, adder_3_cout, subtractor_1_bout, subtractor_2_bout, subtractor_3_bout;
  wire [3:0] divider_1_rem, divider_2_rem, divider_3_rem, multiplier_1_cout, multiplier_2_cout,
       multiplier_3_cout;

  Adder #(.width(4)) adder_1 (.a(in_4), .b(in_6), .out(out_23), .cin(in_2), .cout(adder_1_cout));
  Adder #(.width(4)) adder_2 (.a(in_8), .b(in_10), .out(out_27), .cin(adder_1_cout), .cout(adder_2_cout));
  Adder #(.width(4)) adder_3 (.a(in_14), .b(in_16), .out(out_34), .cin(adder_2_cout), .cout(adder_3_cout));
  Adder #(.width(4)) adder_4 (.a(in_18), .b(in_20), .out(out_38), .cin(adder_3_cout), .cout(out_42));
  Subtractor #(.width(4)) subtractor_1 (.a(in_4), .b(in_6), .out(out_24), .bin(in_2), .bout(subtractor_1_bout));
  Subtractor #(.width(4)) subtractor_2 (
    .a(in_8), .b(in_10), .out(out_28), .bin(subtractor_1_bout), .bout(subtractor_2_bout));
  Subtractor #(.width(4)) subtractor_3 (
    .a(in_14), .b(in_16), .out(out_35), .bin(subtractor_2_bout), .bout(subtractor_3_bout));
  Subtractor #(.width(4)) subtractor_4 (.a(in_18), .b(in_20), .out(out_39), .bin(subtractor_3_bout), .bout(out_43));
  Multiplier #(.width(4)) multiplier_1 (.a(in_3), .b(in_5), .out(out_21), .cin(in_1), .cout(multiplier_1_cout));
  Multiplier #(.width(4)) multiplier_2 (
    .a(in_7), .b(in_9), .out(out_25), .cin(multiplier_1_cout), .cout(multiplier_2_cout));
  Multiplier #(.width(4)) multiplier_3 (
    .a(in_13), .b(in_15), .out(out_32), .cin(multiplier_2_cout), .cout(multiplier_3_cout));
  Multiplier #(.width(4)) multiplier_4 (.a(in_17), .b(in_19), .out(out_36), .cin(multiplier_3_cout), .cout(out_40));
  Divider #(.width(4)) divider_1 (.a(in_3), .b(in_5), .out(out_22), .upper(in_1), .rem(divider_1_rem));
  Divider #(.width(4)) divider_2 (.a(in_7), .b(in_9), .out(out_26), .upper(divider_1_rem), .rem(divider_2_rem));
  Divider #(.width(4)) divider_3 (.a(in_13), .b(in_15), .out(out_33), .upper(divider_2_rem), .rem(divider_3_rem));
  Divider #(.width(4)) divider_4 (.a(in_17), .b(in_19), .out(out_37), .upper(divider_3_rem), .rem(out_41));
  Comparator #(.width(4)) comparator_1 (.a(in_11), .b(in_12), .gt(out_29), .eq(out_30), .lt(out_31));
endmodule
