// Logisim project FINAL CALCULATOR.circ as structural Verilog: 1 circuit, main circuit main
module main (
  input  in_1,
  input  [3:0] in_2,
  input  [3:0] in_3,
  input  in_4,
  input  [3:0] in_5,
  input  [3:0] in_6,
  input  [1:0] in_7,
  output [3:0] out_8
);

  wire [3:0] adder_1_out, divider_1_out, multiplier_1_out, subtractor_1_out;

  Adder #(.width(4)) adder_1 (.a(in_2), .b(in_3), .out(adder_1_out), .cin(in_1));  // open: cout
  Subtractor #(.width(4)) subtractor_1 (.a(in_2), .b(in_3), .out(subtractor_1_out), .bin(in_4));  // open: bout
  Multiplier #(.width(4)) multiplier_1 (.a(in_2), .b(in_3), .out(multiplier_1_out), .cin(in_5));  // open: cout
  Divider #(.width(4)) divider_1 (.a(in_2), .b(in_3), .out(divider_1_out), .upper(in_6));  // open: rem
  Multiplexer #(.select(2), .width(4)) multiplexer_1 (
    .in0(adder_1_out), .in1(subtractor_1_out), .in2(multiplier_1_out), .in3(divider_1_out), .out(out_8),
    .sel(in_7));  // open: en
endmodule
